// Logisim project cpu.circ as structural Verilog: 1 circuit, main circuit cpu
module cpu (
  input  clk,
  input  [31:0] Instruction,
  input  [31:0] MemReadData,
  output [31:0] MemAddress,
  output [31:0] ProgramCounter,
  output [31:0] ra,
  output [31:0] sp,
  output [31:0] t0,
  output [31:0] t1,
  output [31:0] t2,
  output [31:0] s0,
  output [31:0] s1,
  output [31:0] a0,
  output [3:0] MemWriteMask,
  output [31:0] MemWriteData
);

  wire ASel, BrEq, BrLt, BrUn, BSel, control_logic_1_regwen, PCsel;
  wire [2:0] control_logic_1_immsel;
  wire [3:0] ALUSel;
  wire [31:0] adder_1_out, alu_out, Immediate, multiplexer_1_out, multiplexer_2_out, multiplexer_3_out,
       ReadData1, ReadData2;

  Adder #(.width(32)) adder_1 (.a(ProgramCounter), .b(32'h4), .out(adder_1_out));  // open: cin, cout
  Multiplexer #(.width(32)) multiplexer_1 (.in0(adder_1_out), .in1(alu_out), .out(multiplexer_1_out), .sel(PCsel));
  Register #(.width(32)) PC (.D(multiplexer_1_out), .clk(clk), .Q(ProgramCounter));  // open: en, clr
  control_logic control_logic_1 (
    .Instruction(Instruction), .BrEq(BrEq), .BrLt(BrLt), .PCSel(PCsel), .RegWEn(control_logic_1_regwen),
    .ImmSel(control_logic_1_immsel), .BrUn(BrUn), .ASel(ASel), .BSel(BSel), .ALUSel(ALUSel));  // open: MemRW, WBSel
  regfile regfile_1 (
    .ReadIndex1(Instruction[19:15]), .ReadIndex2(Instruction[24:20]), .WriteIndex(Instruction[11:7]),
    .WriteData(alu_out), .RegWEn(control_logic_1_regwen), .clk(clk), .ra(ra), .sp(sp), .t0(t0), .t1(t1),
    .t2(t2), .s0(s0), .s1(s1), .a0(a0), .ReadData1(ReadData1), .ReadData2(ReadData2));
  imm_gen imm_gen_1 (.Instruction(Instruction), .ImmSel(control_logic_1_immsel), .Immediate(Immediate));
  Multiplexer #(.width(32)) multiplexer_2 (.in0(ReadData1), .in1(ProgramCounter), .out(multiplexer_2_out), .sel(ASel));
  Multiplexer #(.width(32)) multiplexer_3 (.in0(ReadData2), .in1(Immediate), .out(multiplexer_3_out), .sel(BSel));
  // partial_store partial_store_1: pin names not known
  // partial_load partial_load_1: pin names not known
  alu alu_1 (.A(multiplexer_2_out), .B(multiplexer_3_out), .ALUSel(ALUSel), .ALUResult(alu_out));
  branch_comp branch_comp_1 (.BrData1(ReadData1), .BrData2(ReadData2), .BrUn(BrUn), .BrEq(BrEq), .BrLt(BrLt));

  // Other names for the same wires on the sheet: wdata[31:0] = alu_out

  // Notes on the sheet:
  //   To IMEM
  //   IMEM (do **NOT** move this)
  //   From IMEM
  //   Inputs/Outputs for testing. Do **NOT** move these.
  //   It is OK to move the PC, RegFile, ALU, MEM, Branch Comp, Imm Gen, Partial Load, Partial Store and Control Logic to wherever is most convenient for you when constructing your CPU, and to delete this text
  //   To DMEM
  //   DMEM (do **NOT** move this)
  //   From DMEM
endmodule
